# Fritzing sketch Tracker+Extension (saved by Fritzing 0.9.3b)
circuit board: 11.26cm x 3cm

parts:
  part = Schottky Diode [part_number=1N5817 package="300 mil [THT]"]
  part_2 = Schottky Diode [part_number=1N5817 package="300 mil [THT]"]
  part_3 = Header 1 [package=1x01_offset]
  part_4 = Header 1 [package=1x01_offset]
  part_5 = Resistor [tolerance=±5% resistance=220 package=THT]
  part_6 = Triple Axis Gyro Breakout ITG-3200
  part_7 = TP4056 [chip_label=TP4056 package="DIP (Dual Inline) [THT]"]
  part_8 = WeMos D1 Mini
  part_9 = Header 4 [package=jst-4-pth]
  part_10 = SPST Switch [package=switch-spdt]
  part_11 = Triple Axis Gyro Breakout ITG-3200
  part_12 = Header 4 [package=jst-4-pth]

nets:
  N1: part.cathode, part_2.cathode, part_8.5V
  N2: part.anode, part_7.pin1
  N3: part_2.anode, part_7.pin3
  N4: part_3.1, part_5.Pin_0, part_7.pin4
  N5: part_4.1, part_7.pin5
  N6: part_5.Pin_1, part_8.A0
  N7: part_6.B, part_8.D2, part_9.4
  N8: part_6.INT, part_8.D1, part_9.3
  N9: part_6.SDA, part_8.3V3, part_9.1
  N10: part_7.pin6, part_10.S
  N11: part_11.B, part_12.4
  N12: part_11.INT, part_12.3
  GND: part_11.GND, part_12.GND
  N13: part_11.SDA, part_12.1

notes:
  @pelide36
  @_andrea.dipalma
  3,3 GND SCL SDA
  scemo chi
  legge
  Batt+
  Batt-

custom parts:
  Triple Axis Gyro Breakout ITG-3200: Description: This is a breakout board for InvenSense's ITG-3200, a groundbreaking triple-axis, digital output gyroscope. The ITG-3200 features three 16-bit analog-to-digital converters (ADCs) for digitizing the gyro outputs, a user-selectable internal low-pass filter bandwidth, and a Fast-Mode I2C (400kHz) interface. Additional features include an embedded temperature sensor and a 2% accurate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
  TP4056: A DIP stand-in part for whatever IC you want. With 6 pins on a 300mil dual inline package (DIP) footprint.
  WeMos D1 Mini: The D1 mini is a mini wifi board based on ESP-8266EX.
  Header 4: Header 4 Standard 4-pin 0.1 header. Use with straight break away headers (SKU : PRT-00116), right angle break away headers (PRT-00553), swiss pins (PRT-00743), machine pins (PRT-00117), and female headers (PRT-00115). Molex polarized connector foot print use with SKU : PRT-08231 with associated crimp pins and housings. 1MM SMD Version SKU: PRT-10208
  SPST Switch: SPST Switch Simple slide switch. Spark Fun Electronics SKU : COM-00102
