# Fritzing sketch extension (saved by Fritzing 0.9.3b)
circuit board: 2.07935cm x 2.37116cm

parts:
  part = Triple Axis Gyro Breakout ITG-3200
  part_2 = Header 4 [package=jst-4-pth]

nets:
  N1: part.B, part_2.4
  N2: part.INT, part_2.3
  GND: part.GND, part_2.GND
  N3: part.SDA, part_2.1

notes:
  3,3 GND SCL SDA
  @_andrea.dipalma
  @pelide36

custom parts:
  Triple Axis Gyro Breakout ITG-3200: Description: This is a breakout board for InvenSense's ITG-3200, a groundbreaking triple-axis, digital output gyroscope. The ITG-3200 features three 16-bit analog-to-digital converters (ADCs) for digitizing the gyro outputs, a user-selectable internal low-pass filter bandwidth, and a Fast-Mode I2C (400kHz) interface. Additional features include an embedded temperature sensor and a 2% accurate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
  Header 4: Header 4 Standard 4-pin 0.1 header. Use with straight break away headers (SKU : PRT-00116), right angle break away headers (PRT-00553), swiss pins (PRT-00743), machine pins (PRT-00117), and female headers (PRT-00115). Molex polarized connector foot print use with SKU : PRT-08231 with associated crimp pins and housings. 1MM SMD Version SKU: PRT-10208
